# Fritzing sketch Schematic (saved by Fritzing 0.9.3b)
breadboards: 1

parts:
  Q1 = NPN-Transistor [package="TO92 [THT]"]
  U1 = RELAY [part_number=JQC-3FF package=OJ]
  V1 = AC Power [voltage=240V frequency=60]
  (GLASS) = DIODE-ZENER [part_number=5V package=diode-zener]
  S2 = SWITCH-MOMENTARY-2 [package=tactile_switch_smd-2]
  IC1 = IC, DIP package, 14 pins [chip_label=HS2300-P]
  LED1 = LED - 3mm [color="Red (633nm)" part_number=6 package="3 mm [THT]"]
  LED2 = LED - 3mm [color="Red (633nm)" part_number=5 package="3 mm [THT]"]
  LED3 = LED - 3mm [color="Red (633nm)" part_number=4 package="3 mm [THT]"]
  LED4 = LED - 3mm [color="Red (633nm)" part_number=2 package="3 mm [THT]"]
  LED5 = LED - 3mm [color="Red (633nm)" part_number=3 package="3 mm [THT]"]
  LED6 = LED - 3mm [color="Red (633nm)" part_number=1 package="3 mm [THT]"]
  WeMos_D1_Mini1 = WeMos D1 Mini
  IC2 = IC, DIP package, 4 pins [chip_label=Rectifier part_number=MB10F]
  1SMA4749A = DIODE-ZENER [part_number=24V package=diode-zener]
  OUTLET = AC Power [voltage=240V frequency=60]
  R1 = Resistor [tolerance=±5% resistance=2.2k package=THT]
  R2 = Resistor [tolerance=±5% resistance=2.2k package=THT]
  R3 = Resistor [tolerance=±5% resistance=22k package=THT]
  R4 = Resistor [tolerance=±5% resistance=100 power=1W package=THT]
  R5 = Resistor [tolerance=±5% resistance=1M power=0.25W package="1206 [SMD]"]
  (X=1411) = Film/Foil Capacitor [capacitance=100nF voltage=35V part_number=0.47uF package="15mm [THT, pp]"]

nets:
  GND: Q1.E, (GLASS).A, S2.1, IC1.pin4, IC1.pin7, WeMos_D1_Mini1.G, IC2.pin4, 1SMA4749A.A
  N1: Q1.B, R3.Pin_0
  N2: Q1.C, U1.COIL1
  N3: U1.COIL2, IC2.pin3, 1SMA4749A.C, R1.Pin_0
  N4: U1.MAIN, OUTLET.V+
  N5: U1.NO, V1.V+, IC2.pin2
  N6: V1.V-, OUTLET.V-, R4.Pin_1
  N7: (GLASS).C, IC1.pin11, WeMos_D1_Mini1.3V3, R1.Pin_1, R2.Pin_0
  N8: S2.2, IC1.pin1, IC1.pin2
  N9: IC1.pin6, WeMos_D1_Mini1.D0, R3.Pin_1
  N10: IC1.pin8, LED6.cathode
  N11: IC1.pin9, LED4.cathode
  N12: IC1.pin10, LED5.cathode
  N13: IC1.pin12, LED3.cathode
  N14: IC1.pin13, LED1.cathode
  N15: IC1.pin14, LED2.cathode
  N16: LED1.anode, LED2.anode, LED3.anode, LED4.anode, LED5.anode, LED6.anode, R2.Pin_1
  N17: IC2.pin1, R5.Pin_1, (X=1411).+
  N18: R4.Pin_0, R5.Pin_0, (X=1411).-

notes:
  Original circuit (roughly)
  New MCU (red wires)
  NOTE: Must break connection   here
  Many caps and resistors ignored
  Combined impedance 1409ohm
